# Fritzing sketch 2025-02-03 - Raspi-KEVIN-Garage (saved by Fritzing 0.9.3b)
breadboards: 1
stripboards: 1
perfboards: 1

parts:
  Raspberry_Pi_1 = Raspberry Pi 4 [part_number=RPI-4-b]
  Q1 = PNP-Transistor [package="TO92 [THT]"]
  Q2 = PNP-Transistor [package="TO92 [THT]"]
  Q3 = PNP-Transistor [package="TO92 [THT]"]
  R1 = Resistor [tolerance=±10% resistance=330 package=THT]
  R2 = Resistor [tolerance=±10% resistance=330 package=THT]
  S1 = Pushbutton [package="[THT]"]
  R3 = Resistor [tolerance=±10% resistance=330 package=THT]
  S2 = Pushbutton [package="[THT]"]
  BAT1 = Battery Holders [package=battcon_20mm]  # not connected

nets:
  N1: Raspberry_Pi_1.GPIO22, R2.Pin_1
  N2: Raspberry_Pi_1.GPIO24, R1.Pin_0
  N3: Raspberry_Pi_1.GPIO23, R3.Pin_0
  N4: Raspberry_Pi_1.GND, Q1.E
  N5: Q1.B, R2.Pin_0
  N6: Q2.E, Q2.C, S2.Pin_1, S2.Pin_2, S2.Pin_3, S2.Pin_4
  N7: Q2.B, R3.Pin_1
  N8: Q3.E, Q3.C, S1.Pin_1, S1.Pin_2, S1.Pin_3, S1.Pin_4
  N9: Q3.B, R1.Pin_1

notes:
  Garage2
  Alimentation
  Garage1
  Télécommande (face)
  Télécommande (verso)
  rouge : alimentation 5V
  noir : neutre
  jaune : GPIO out 22
  bleu : GPIO out 23
  vert : GPIO out 24

custom parts:
  Raspberry Pi 4: The RPi4, a faster version of the awesome Raspberry Pi 2 B ARM Board with 40 pin gpio. Ready for special Raspberry Pi B+ and RPi2 Hat (Hardware attached (on) top)

// code stored in the sketch: Untitled.ino
import RPi.GPIO as GPIO
import time



GPIO.setmode(GPIO.BCM)


TRIG = 23
ECHO = 24
LED1 = 13
LED2 = 19
buzzer = 26
motor1a= 3
motor1b= 4
motor2a= 20
motor2b= 21
motor= 25
i=0


GPIO.setup(TRIG,GPIO.OUT)
GPIO.setup(ECHO,GPIO.IN)


GPIO.setup(LED1,GPIO.OUT)
GPIO.setup(LED2,GPIO.OUT)
GPIO.setup(buzzer,GPIO.OUT)
GPIO.setup(motor1a,GPIO.OUT)
GPIO.setup(motor1b,GPIO.OUT)
GPIO.setup(motor2a,GPIO.OUT)
GPIO.setup(motor2b,GPIO.OUT)
GPIO.setup(motor,GPIO.OUT)






GPIO.output(TRIG, False)
print("Calibrating.....")
print("Place the object......")




while True:
    GPIO.output(TRIG, True)
    time.sleep(0.00001)
    GPIO.output(TRIG, False)


    while GPIO.input(ECHO)==0:
        pulse_start = time.time()


    while GPIO.input(ECHO)==1:
        pulse_end = time.time()


    pulse_duration = pulse_end - pulse_start


    distance = pulse_duration * 17150


    distance = round(distance+1.15, 2)
  
    if distance<=10:
        print("distance:",distance,"cm")
        GPIO.output(LED1,GPIO.HIGH)
        GPIO.output(LED2,GPIO.LOW)
        GPIO.output(buzzer,GPIO.HIGH)
        GPIO.output(motor1a,GPIO.HIGH)
        GPIO.output(motor1b,GPIO.LOW)
        GPIO.output(motor2a,GPIO.HIGH)
        GPIO.output(motor2b,GPIO.LOW)
        GPIO.output(motor,GPIO.HIGH)
        time.sleep(1)
        GPIO.output(buzzer,GPIO.LOW)
        
    else:
        print("place the object....")
        GPIO.output(LED1,GPIO.LOW)
        GPIO.output(LED2,GPIO.HIGH)
        GPIO.output(buzzer,GPIO.LOW)
        GPIO.output(motor1a,GPIO.LOW)
        GPIO.output(motor1b,GPIO.HIGH)
        GPIO.output(motor2a,GPIO.LOW)
        GPIO.output(motor2b,GPIO.HIGH)
        GPIO.output(motor,GPIO.HIGH)
